// Logisim project ikramass2.circ as structural Verilog: 11 circuits, main circuit main
module main (
  input  [1:0] Control,
  input  [18:0] A,
  input  [18:0] B,
  output [18:0] Result,
  output Zero,
  output Negative,
  output Overflow,
  output Carry
);

  _19_bit_ALU u_19_bit_alu_1 (
    .A(A), .B(B), .Result(Result), .Zero(Zero), .Negative(Negative), .Overflow(Overflow), .Carry(Carry),
    .Control0(Control[1]), .Control1(Control[0]));
endmodule

// 19-bit AND
module _19_bit_and (
  input  [18:0] A,
  input  [18:0] B,
  output [18:0] Result
);

  and and_1 (Result[0], A[0], B[0]);
  and and_2 (Result[1], A[1], B[1]);
  and and_3 (Result[2], A[2], B[2]);
  and and_4 (Result[3], A[3], B[3]);
  and and_5 (Result[4], A[4], B[4]);
  and and_6 (Result[5], A[5], B[5]);
  and and_7 (Result[6], A[6], B[6]);
  and and_8 (Result[7], A[7], B[7]);
  and and_9 (Result[8], A[8], B[8]);
  and and_10 (Result[9], A[9], B[9]);
  and and_11 (Result[10], A[10], B[10]);
  and and_12 (Result[11], A[11], B[11]);
  and and_13 (Result[12], A[12], B[12]);
  and and_14 (Result[13], A[13], B[13]);
  and and_15 (Result[14], A[14], B[14]);
  and and_16 (Result[15], A[15], B[15]);
  and and_17 (Result[16], A[16], B[16]);
  and and_18 (Result[17], A[17], B[17]);
  and and_19 (Result[18], A[18], B[18]);
endmodule

// 19-bit OR
module _19_bit_OR (
  input  [18:0] A,
  input  [18:0] B,
  output [18:0] Result
);

  or or_1 (Result[0], A[0], B[0]);
  or or_2 (Result[1], A[1], B[1]);
  or or_3 (Result[2], A[2], B[2]);
  or or_4 (Result[3], A[3], B[3]);
  or or_5 (Result[4], A[4], B[4]);
  or or_6 (Result[5], A[5], B[5]);
  or or_7 (Result[6], A[6], B[6]);
  or or_8 (Result[7], A[7], B[7]);
  or or_9 (Result[8], A[8], B[8]);
  or or_10 (Result[9], A[9], B[9]);
  or or_11 (Result[10], A[10], B[10]);
  or or_12 (Result[11], A[11], B[11]);
  or or_13 (Result[12], A[12], B[12]);
  or or_14 (Result[13], A[13], B[13]);
  or or_15 (Result[14], A[14], B[14]);
  or or_16 (Result[15], A[15], B[15]);
  or or_17 (Result[16], A[16], B[16]);
  or or_18 (Result[17], A[17], B[17]);
  or or_19 (Result[18], A[18], B[18]);
endmodule

module Full_adder (
  input  Carry_in,
  input  A,
  input  B,
  output Result,
  output Carry_out
);

  wire and_1_out, and_2_out, xor_1_out;

  and and_1 (and_1_out, B, A);
  xor xor_1 (xor_1_out, A, B);
  or or_1 (Carry_out, and_1_out, and_2_out);
  and and_2 (and_2_out, xor_1_out, Carry_in);
  xor xor_2 (Result, Carry_in, xor_1_out);
endmodule

module _19_bit_full_adder (
  input  Carry_in,
  input  A0,
  input  B0,
  input  A1,
  input  B1,
  input  A2,
  input  B2,
  input  A3,
  input  B3,
  input  A4,
  input  B4,
  input  A5,
  input  B5,
  input  A6,
  input  B6,
  input  A7,
  input  B7,
  input  A8,
  input  B8,
  input  A9,
  input  B9,
  input  A10,
  input  B10,
  input  A11,
  input  B11,
  input  A12,
  input  B12,
  input  A13,
  input  B13,
  input  A14,
  input  B14,
  input  A15,
  input  B15,
  input  A16,
  input  B16,
  input  A17,
  input  B17,
  input  A18,
  input  B18,
  input  A19,
  input  B19,
  input  A20,
  input  B20,
  input  A21,
  input  B21,
  input  A22,
  input  B22,
  input  A23,
  input  B23,
  input  A24,
  input  B24,
  input  A25,
  input  B25,
  input  A26,
  input  B26,
  input  A27,
  input  B27,
  input  A28,
  input  B28,
  input  A29,
  input  B29,
  input  A30,
  input  B30,
  input  A31,
  input  B31,
  output Result0,
  output Result1,
  output Result2,
  output Result3,
  output Result4,
  output Result5,
  output Result6,
  output Result7,
  output Result8,
  output Result9,
  output Result10,
  output Result11,
  output Result12,
  output Result13,
  output Result14,
  output Result15,
  output Result16,
  output Result17,
  output Result18,
  output Result19,
  output Result20,
  output Result21,
  output Result22,
  output Result23,
  output Result24,
  output Result25,
  output Result26,
  output Result27,
  output Result28,
  output Result29,
  output Result30,
  output Result31,
  output Carry
);

  wire full_adder_1_carry_out, full_adder_2_carry_out, full_adder_3_carry_out, full_adder_4_carry_out,
       full_adder_5_carry_out, full_adder_6_carry_out, full_adder_7_carry_out, full_adder_8_carry_out,
       full_adder_9_carry_out, full_adder_10_carry_out, full_adder_11_carry_out, full_adder_12_carry_out,
       full_adder_13_carry_out, full_adder_14_carry_out, full_adder_15_carry_out, full_adder_16_carry_out,
       full_adder_17_carry_out, full_adder_18_carry_out, full_adder_19_carry_out, full_adder_20_carry_out,
       full_adder_21_carry_out, full_adder_22_carry_out, full_adder_23_carry_out, full_adder_24_carry_out,
       full_adder_25_carry_out, full_adder_26_carry_out, full_adder_27_carry_out, full_adder_28_carry_out,
       full_adder_29_carry_out, full_adder_30_carry_out, full_adder_31_carry_out;

  Full_adder full_adder_1 (.Carry_in(Carry_in), .A(A0), .B(B0), .Result(Result0), .Carry_out(full_adder_1_carry_out));
  Full_adder full_adder_2 (
    .Carry_in(full_adder_1_carry_out), .A(A1), .B(B1), .Result(Result1), .Carry_out(full_adder_2_carry_out));
  Full_adder full_adder_3 (
    .Carry_in(full_adder_2_carry_out), .A(A2), .B(B2), .Result(Result2), .Carry_out(full_adder_3_carry_out));
  Full_adder full_adder_4 (
    .Carry_in(full_adder_3_carry_out), .A(A3), .B(B3), .Result(Result3), .Carry_out(full_adder_4_carry_out));
  Full_adder full_adder_5 (
    .Carry_in(full_adder_4_carry_out), .A(A4), .B(B4), .Result(Result4), .Carry_out(full_adder_5_carry_out));
  Full_adder full_adder_6 (
    .Carry_in(full_adder_5_carry_out), .A(A5), .B(B5), .Result(Result5), .Carry_out(full_adder_6_carry_out));
  Full_adder full_adder_7 (
    .Carry_in(full_adder_6_carry_out), .A(A6), .B(B6), .Result(Result6), .Carry_out(full_adder_7_carry_out));
  Full_adder full_adder_8 (
    .Carry_in(full_adder_7_carry_out), .A(A7), .B(B7), .Result(Result7), .Carry_out(full_adder_8_carry_out));
  Full_adder full_adder_9 (
    .Carry_in(full_adder_8_carry_out), .A(A8), .B(B8), .Result(Result8), .Carry_out(full_adder_9_carry_out));
  Full_adder full_adder_10 (
    .Carry_in(full_adder_9_carry_out), .A(A9), .B(B9), .Result(Result9), .Carry_out(full_adder_10_carry_out));
  Full_adder full_adder_11 (
    .Carry_in(full_adder_10_carry_out), .A(A10), .B(B10), .Result(Result10),
    .Carry_out(full_adder_11_carry_out));
  Full_adder full_adder_12 (
    .Carry_in(full_adder_11_carry_out), .A(A11), .B(B11), .Result(Result11),
    .Carry_out(full_adder_12_carry_out));
  Full_adder full_adder_13 (
    .Carry_in(full_adder_12_carry_out), .A(A12), .B(B12), .Result(Result12),
    .Carry_out(full_adder_13_carry_out));
  Full_adder full_adder_14 (
    .Carry_in(full_adder_13_carry_out), .A(A13), .B(B13), .Result(Result13),
    .Carry_out(full_adder_14_carry_out));
  Full_adder full_adder_15 (
    .Carry_in(full_adder_14_carry_out), .A(A14), .B(B14), .Result(Result14),
    .Carry_out(full_adder_15_carry_out));
  Full_adder full_adder_16 (
    .Carry_in(full_adder_15_carry_out), .A(A15), .B(B15), .Result(Result15),
    .Carry_out(full_adder_16_carry_out));
  Full_adder full_adder_17 (
    .Carry_in(full_adder_16_carry_out), .A(A16), .B(B16), .Result(Result16),
    .Carry_out(full_adder_17_carry_out));
  Full_adder full_adder_18 (
    .Carry_in(full_adder_17_carry_out), .A(A17), .B(B17), .Result(Result17),
    .Carry_out(full_adder_18_carry_out));
  Full_adder full_adder_19 (
    .Carry_in(full_adder_18_carry_out), .A(A18), .B(B18), .Result(Result18),
    .Carry_out(full_adder_19_carry_out));
  Full_adder full_adder_20 (
    .Carry_in(full_adder_19_carry_out), .A(A19), .B(B19), .Result(Result19),
    .Carry_out(full_adder_20_carry_out));
  Full_adder full_adder_21 (
    .Carry_in(full_adder_20_carry_out), .A(A20), .B(B20), .Result(Result20),
    .Carry_out(full_adder_21_carry_out));
  Full_adder full_adder_22 (
    .Carry_in(full_adder_21_carry_out), .A(A21), .B(B21), .Result(Result21),
    .Carry_out(full_adder_22_carry_out));
  Full_adder full_adder_23 (
    .Carry_in(full_adder_22_carry_out), .A(A22), .B(B22), .Result(Result22),
    .Carry_out(full_adder_23_carry_out));
  Full_adder full_adder_24 (
    .Carry_in(full_adder_23_carry_out), .A(A23), .B(B23), .Result(Result23),
    .Carry_out(full_adder_24_carry_out));
  Full_adder full_adder_25 (
    .Carry_in(full_adder_24_carry_out), .A(A24), .B(B24), .Result(Result24),
    .Carry_out(full_adder_25_carry_out));
  Full_adder full_adder_26 (
    .Carry_in(full_adder_25_carry_out), .A(A25), .B(B25), .Result(Result25),
    .Carry_out(full_adder_26_carry_out));
  Full_adder full_adder_27 (
    .Carry_in(full_adder_26_carry_out), .A(A26), .B(B26), .Result(Result26),
    .Carry_out(full_adder_27_carry_out));
  Full_adder full_adder_28 (
    .Carry_in(full_adder_27_carry_out), .A(A27), .B(B27), .Result(Result27),
    .Carry_out(full_adder_28_carry_out));
  Full_adder full_adder_29 (
    .Carry_in(full_adder_28_carry_out), .A(A28), .B(B28), .Result(Result28),
    .Carry_out(full_adder_29_carry_out));
  Full_adder full_adder_30 (
    .Carry_in(full_adder_29_carry_out), .A(A29), .B(B29), .Result(Result29),
    .Carry_out(full_adder_30_carry_out));
  Full_adder full_adder_31 (
    .Carry_in(full_adder_30_carry_out), .A(A30), .B(B30), .Result(Result30),
    .Carry_out(full_adder_31_carry_out));
  Full_adder full_adder_32 (.Carry_in(full_adder_31_carry_out), .A(A31), .B(B31), .Result(Result31), .Carry_out(Carry));
endmodule

// FA
module _19_bit_full_adder_concise (
  input  Carry_in,
  input  [18:0] A,
  input  [18:0] B,
  output [18:0] Result,
  output Carry
);

  wire full_adder_1_carry_out, full_adder_2_carry_out, full_adder_3_carry_out, full_adder_4_carry_out,
       full_adder_5_carry_out, full_adder_6_carry_out, full_adder_7_carry_out, full_adder_8_carry_out,
       full_adder_9_carry_out, full_adder_10_carry_out, full_adder_11_carry_out, full_adder_12_carry_out,
       full_adder_13_carry_out, full_adder_14_carry_out, full_adder_15_carry_out, full_adder_16_carry_out,
       full_adder_17_carry_out, full_adder_18_carry_out;

  Full_adder full_adder_1 (
    .Carry_in(Carry_in), .A(A[0]), .B(B[0]), .Result(Result[0]), .Carry_out(full_adder_1_carry_out));
  Full_adder full_adder_2 (
    .Carry_in(full_adder_1_carry_out), .A(A[1]), .B(B[1]), .Result(Result[1]),
    .Carry_out(full_adder_2_carry_out));
  Full_adder full_adder_3 (
    .Carry_in(full_adder_2_carry_out), .A(A[2]), .B(B[2]), .Result(Result[2]),
    .Carry_out(full_adder_3_carry_out));
  Full_adder full_adder_4 (
    .Carry_in(full_adder_3_carry_out), .A(A[3]), .B(B[3]), .Result(Result[3]),
    .Carry_out(full_adder_4_carry_out));
  Full_adder full_adder_5 (
    .Carry_in(full_adder_4_carry_out), .A(A[4]), .B(B[4]), .Result(Result[4]),
    .Carry_out(full_adder_5_carry_out));
  Full_adder full_adder_6 (
    .Carry_in(full_adder_5_carry_out), .A(A[5]), .B(B[5]), .Result(Result[5]),
    .Carry_out(full_adder_6_carry_out));
  Full_adder full_adder_7 (
    .Carry_in(full_adder_6_carry_out), .A(A[6]), .B(B[6]), .Result(Result[6]),
    .Carry_out(full_adder_7_carry_out));
  Full_adder full_adder_8 (
    .Carry_in(full_adder_7_carry_out), .A(A[7]), .B(B[7]), .Result(Result[7]),
    .Carry_out(full_adder_8_carry_out));
  Full_adder full_adder_9 (
    .Carry_in(full_adder_8_carry_out), .A(A[8]), .B(B[8]), .Result(Result[8]),
    .Carry_out(full_adder_9_carry_out));
  Full_adder full_adder_10 (
    .Carry_in(full_adder_9_carry_out), .A(A[9]), .B(B[9]), .Result(Result[9]),
    .Carry_out(full_adder_10_carry_out));
  Full_adder full_adder_11 (
    .Carry_in(full_adder_10_carry_out), .A(A[10]), .B(B[10]), .Result(Result[10]),
    .Carry_out(full_adder_11_carry_out));
  Full_adder full_adder_12 (
    .Carry_in(full_adder_11_carry_out), .A(A[11]), .B(B[11]), .Result(Result[11]),
    .Carry_out(full_adder_12_carry_out));
  Full_adder full_adder_13 (
    .Carry_in(full_adder_12_carry_out), .A(A[12]), .B(B[12]), .Result(Result[12]),
    .Carry_out(full_adder_13_carry_out));
  Full_adder full_adder_14 (
    .Carry_in(full_adder_13_carry_out), .A(A[13]), .B(B[13]), .Result(Result[13]),
    .Carry_out(full_adder_14_carry_out));
  Full_adder full_adder_15 (
    .Carry_in(full_adder_14_carry_out), .A(A[14]), .B(B[14]), .Result(Result[14]),
    .Carry_out(full_adder_15_carry_out));
  Full_adder full_adder_16 (
    .Carry_in(full_adder_15_carry_out), .A(A[15]), .B(B[15]), .Result(Result[15]),
    .Carry_out(full_adder_16_carry_out));
  Full_adder full_adder_17 (
    .Carry_in(full_adder_16_carry_out), .A(A[16]), .B(B[16]), .Result(Result[16]),
    .Carry_out(full_adder_17_carry_out));
  Full_adder full_adder_18 (
    .Carry_in(full_adder_17_carry_out), .A(A[17]), .B(B[17]), .Result(Result[17]),
    .Carry_out(full_adder_18_carry_out));
  Full_adder full_adder_19 (
    .Carry_in(full_adder_18_carry_out), .A(A[18]), .B(B[18]), .Result(Result[18]), .Carry_out(Carry));
endmodule

module _19_bit_xor (
  input  Control,
  input  [18:0] B,
  output [18:0] Result
);

  wire [18:0] bit_extender_1_out;

  assign bit_extender_1_out = {{18{Control}}, Control};  // Bit_Extender bit_extender_1
  xor xor_1 (Result[0], bit_extender_1_out[0], B[0]);
  xor xor_2 (Result[1], bit_extender_1_out[1], B[1]);
  xor xor_3 (Result[2], bit_extender_1_out[2], B[2]);
  xor xor_4 (Result[3], bit_extender_1_out[3], B[3]);
  xor xor_5 (Result[4], bit_extender_1_out[4], B[4]);
  xor xor_6 (Result[5], bit_extender_1_out[5], B[5]);
  xor xor_7 (Result[6], bit_extender_1_out[6], B[6]);
  xor xor_8 (Result[7], bit_extender_1_out[7], B[7]);
  xor xor_9 (Result[8], bit_extender_1_out[8], B[8]);
  xor xor_10 (Result[9], bit_extender_1_out[9], B[9]);
  xor xor_11 (Result[10], bit_extender_1_out[10], B[10]);
  xor xor_12 (Result[11], bit_extender_1_out[11], B[11]);
  xor xor_13 (Result[12], bit_extender_1_out[12], B[12]);
  xor xor_14 (Result[13], bit_extender_1_out[13], B[13]);
  xor xor_15 (Result[14], bit_extender_1_out[14], B[14]);
  xor xor_16 (Result[15], bit_extender_1_out[15], B[15]);
  xor xor_17 (Result[16], bit_extender_1_out[16], B[16]);
  xor xor_18 (Result[17], bit_extender_1_out[17], B[17]);
  xor xor_19 (Result[18], bit_extender_1_out[18], B[18]);
endmodule

// 32-bit \nADD/SUB
module Add_sub (
  input  Sub,
  input  [18:0] A,
  input  [18:0] B,
  output [18:0] Result,
  output Carry,
  output Overflow
);

  wire and_1_out, and_2_out, n18th_bit_out_1__18th_bit, n18th_bit_out_2__18th_bit, n18th_bit_out_3__18th_bit,
       not_1_out, not_2_out, not_3_out;
  wire [18:0] n19_bit_xor_1_result;

  _18th_bit_out u_18th_bit_out_1 (.Input(A), ._18th_bit(n18th_bit_out_1__18th_bit));
  not not_1 (not_1_out, n18th_bit_out_1__18th_bit);
  _18th_bit_out u_18th_bit_out_2 (.Input(B), ._18th_bit(n18th_bit_out_2__18th_bit));
  not not_2 (not_2_out, n18th_bit_out_2__18th_bit);
  _19_bit_xor u_19_bit_xor_1 (.Control(Sub), .Result(n19_bit_xor_1_result), .B(B));
  _19_bit_full_adder_concise u_19_bit_full_adder_concise_1 (
    .Carry(Carry), .Carry_in(Sub), .A(A), .Result(Result), .B(n19_bit_xor_1_result));
  _18th_bit_out u_18th_bit_out_3 (.Input(Result), ._18th_bit(n18th_bit_out_3__18th_bit));
  not not_3 (not_3_out, n18th_bit_out_3__18th_bit);
  and and_1 (and_1_out, not_3_out, n18th_bit_out_2__18th_bit, n18th_bit_out_1__18th_bit);
  and and_2 (and_2_out, n18th_bit_out_3__18th_bit, not_2_out, not_1_out);
  or or_1 (Overflow, and_1_out, and_2_out);

  // Notes on the sheet:
  //   A31
  //   B31
  //   Result 31
endmodule

// 18th
module _18th_bit_out (
  input  [18:0] Input,
  output _18th_bit
);


  assign _18th_bit = Input[18];
endmodule

// Reduce-OR
module _19_bit_reduce_or (
  input  [18:0] Input,
  output Output
);

  wire or_1_out, or_2_out, or_3_out, or_4_out, or_5_out, or_6_out, or_7_out, or_8_out, or_9_out, or_10_out,
       or_11_out, or_12_out, or_13_out, or_14_out, or_15_out, or_16_out, or_17_out;

  or or_1 (or_1_out, Input[0], Input[1]);
  or or_2 (or_2_out, or_1_out, Input[2]);
  or or_3 (or_3_out, or_2_out, Input[3]);
  or or_4 (or_4_out, or_3_out, Input[4]);
  or or_5 (or_5_out, or_4_out, Input[5]);
  or or_6 (or_6_out, or_5_out, Input[6]);
  or or_7 (or_7_out, or_6_out, Input[7]);
  or or_8 (or_8_out, or_7_out, Input[8]);
  or or_9 (or_9_out, or_8_out, Input[9]);
  or or_10 (or_10_out, or_9_out, Input[10]);
  or or_11 (or_11_out, or_10_out, Input[11]);
  or or_12 (or_12_out, or_11_out, Input[12]);
  or or_13 (or_13_out, or_12_out, Input[13]);
  or or_14 (or_14_out, or_13_out, Input[14]);
  or or_15 (or_15_out, or_14_out, Input[15]);
  or or_16 (or_16_out, or_15_out, Input[16]);
  or or_17 (or_17_out, or_16_out, Input[17]);
  or or_18 (Output, or_17_out, Input[18]);
endmodule

module _19_bit_ALU (
  input  Control0,
  input  Control1,
  input  [18:0] A,
  input  [18:0] B,
  output [18:0] Result,
  output Zero,
  output Negative,
  output Overflow,
  output Carry
);

  wire n19_bit_reduce_or_1_output;
  wire [18:0] add_sub_1_result, multiplexer_1_out, n19_bit_and_1_result, n19_bit_or_1_result;

  _19_bit_and u_19_bit_and_1 (.B(A), .A(B), .Result(n19_bit_and_1_result));
  _19_bit_OR u_19_bit_or_1 (.A(A), .Result(n19_bit_or_1_result), .B(B));
  Add_sub add_sub_1 (.Sub(Control0), .A(A), .B(B), .Result(add_sub_1_result), .Carry(Carry), .Overflow(Overflow));
  Multiplexer #(.width(19), .enable("false")) multiplexer_1 (
    .in0(n19_bit_and_1_result), .in1(n19_bit_or_1_result), .out(multiplexer_1_out), .sel(Control0));
  Multiplexer #(.width(19), .enable("false")) multiplexer_2 (
    .in0(multiplexer_1_out), .in1(add_sub_1_result), .out(Result), .sel(Control1));
  _18th_bit_out u_18th_bit_out_1 (.Input(Result), ._18th_bit(Negative));
  _19_bit_reduce_or u_19_bit_reduce_or_1 (.Input(Result), .Output(n19_bit_reduce_or_1_output));
  not not_1 (Zero, n19_bit_reduce_or_1_output);

  // Notes on the sheet:
  //   01 = +
  //   10 = OR
  //   11 = -
  //   00 = AND
endmodule
